# Fritzing sketch robot_dog_schematics (saved by Fritzing 0.9.3b)
breadboards: 1

parts:
  J1 = Basic Force Sensing Resistor (FSR) [package=THT]
  SERVO1 = Tower Pro SG90 servo [part_number=101246]
  Part1 = Adafruit Feather HUZZAH ESP8266 [part_number="Adafruit #2821"]
  Part2 = Breakout Board for Electret Microphone
  J3 = Basic Force Sensing Resistor (FSR) [package=THT]
  J4 = Basic Force Sensing Resistor (FSR) [package=THT]
  J5 = Basic Force Sensing Resistor (FSR) [package=THT]
  IC1 = IC, DIP package, 16 pins [chip_label="IC 4051"]
  R1 = Resistor [tolerance=±5% resistance=22k package="0402 [SMD]"]
  R2 = Resistor [tolerance=±5% resistance=22k package="0402 [SMD]"]
  R3 = Resistor [tolerance=±5% resistance=22k package="0402 [SMD]"]
  R4 = Resistor [tolerance=±5% resistance=22k package="0402 [SMD]"]
  R5 = Resistor [tolerance=±5% resistance=10k package="0402 [SMD]"]
  R6 = Resistor [tolerance=±5% resistance=10k package="0402 [SMD]"]
  R7 = Resistor [tolerance=±5% resistance=10k package="0402 [SMD]"]
  R8 = Resistor [tolerance=±5% resistance=10k package="0402 [SMD]"]
  Grove_Buzzer1 = Grove Buzzer

nets:
  VCC: J1.pin_0, SERVO1.+5V, Part1.3.3V, Part2.VCC, J3.pin_0, J4.pin_0, J5.pin_0, IC1.pin16, Grove_Buzzer1.VCC
  N1: J1.pin_1, R4.Pin_0
  N2: SERVO1.Signal, Part1.GPIO2
  GND: SERVO1.GND, Part1.GND, Part2.GND, IC1.pin6, IC1.pin8, R5.Pin_1, R6.Pin_1, R7.Pin_1, R8.Pin_1, Grove_Buzzer1.GND
  N3: Part1.GPIO12/MISO, IC1.pin11
  N4: Part1.GPIO13/MOSI, IC1.pin10
  N5: Part1.GPIO14/SCK, Grove_Buzzer1.SIG
  N6: Part1.ADC, IC1.pin3
  N7: Part1.GPIO15, IC1.pin9
  N8: J3.pin_1, R1.Pin_0
  N9: J4.pin_1, R2.Pin_0
  N10: J5.pin_1, R3.Pin_0
  N11: IC1.pin12, R4.Pin_1, R8.Pin_0
  N12: IC1.pin13, R3.Pin_1, R7.Pin_0
  N13: IC1.pin14, R2.Pin_1, R6.Pin_0
  N14: IC1.pin15, R1.Pin_1, R5.Pin_0

notes:
  12k resistors
  22k resistors
  Sound detector
  (has both analog and digital pins)

custom parts:
  Tower Pro SG90 servo: Original file by John De Cristofaro http://www.adafruit.com/products/1449 Adafruit Feedback Servo (Small) Edited by: e-radionica.com 28/9/2015
  Adafruit Feather HUZZAH ESP8266: his is the Adafruit Feather HUZZAH ESP8266 - our take on an 'all-in-one' ESP8266 WiFi development board with built in USB and battery charging. Its an ESP8266 WiFi module with all the extras you need, ready to rock! We have other boards in the Feather family, check'em out here. At the Feather HUZZAH's heart is an ESP8266 WiFi microcontroller clocked at 80 MHz and at 3.3V logic. This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
  Grove Buzzer: Buzzer, Grove connector.
